# Fritzing sketch Gesture_control (saved by Fritzing 0.9.1b)
breadboards: 1

parts:
  PART1 = APDS-9960 RGB and Gesture Sensor [part_number=SEN-12787]  # not connected
  Part1 = Bi-Directional Logic Level Converter
  Part2 = Arduino Uno (Rev3)

nets:
  N1: Part1.LV, Part1.HV, Part2.3V3
  N2: Part1.HV4, Part2.A5/SCL
  N3: Part1.HV3, Part2.A4/SDA
  N4: Part1.HV1, Part2.D2

custom parts:
  APDS-9960 RGB and Gesture Sensor: Breakout board for the Avago APDS-9960 proximity, light, RGB, and gesture sensors. Please visit www.sparkfun.com to learn more.
  Bi-Directional Logic Level Converter: Description: If you've ever tried to connect a 3.3V device to a 5V system, you know what a challenge it can be. The SparkFun bi-directional logic level converter is a small device that safely steps down 5V signals to 3.3V AND steps up 3.3V to 5V at the same time. This level converter also works with 2.8V and 1.8V devices. What really separates this Logic level converter from our previous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
